# Fritzing sketch conRoller (saved by Fritzing 0.9.3b)
breadboards: 1

parts:
  Rotary_Encoder = Rotary Encoder [package=THT]
  Teensy_3_2 = Teensy 3.1
  Start_Button = Round Pushbutton
  Fire_Button = Round Pushbutton
  Food_Processor = PowerSwitch Tail II
  Blender = PowerSwitch Tail II

nets:
  N1: Rotary_Encoder.EncoderPinA, Teensy_3_2.D7
  N2: Rotary_Encoder.EncoderPinB, Teensy_3_2.D6
  N3: Teensy_3_2.D12, Food_Processor.+in
  N4: Teensy_3_2.3V3, Start_Button.leg1, Fire_Button.leg1
  N5: Teensy_3_2.D13, Blender.+in
  N6: Teensy_3_2.A1/D15, Fire_Button.leg0
  N7: Teensy_3_2.A2/D16, Start_Button.leg0
