# Fritzing sketch pulpPads (saved by Fritzing 0.9.3b)

parts:
  Part1 = TRRS 3.5mm Jack Breakout
  Part2 = TRRS 3.5mm Jack Breakout
  Part3 = TRRS 3.5mm Jack Breakout
  Part4 = TRRS 3.5mm Jack Breakout
  Teensy_3_2 = Teensy 3.1
  R1 = Resistor [tolerance=±5% resistance=220 package="0402 [SMD]"]
  R2 = Resistor [tolerance=±5% resistance=220 package="0402 [SMD]"]
  R4 = Resistor [tolerance=±5% resistance=220 package="0402 [SMD]"]
  R5 = Resistor [tolerance=±5% resistance=220 package="0402 [SMD]"]
  R6 = Resistor [tolerance=±5% resistance=220 package="0402 [SMD]"]
  R7 = Resistor [tolerance=±5% resistance=220 package="0402 [SMD]"]
  R8 = Resistor [tolerance=±5% resistance=220 package="0402 [SMD]"]
  R9 = Resistor [tolerance=±5% resistance=220 package="0402 [SMD]"]
  R10 = Resistor [tolerance=±5% resistance=220 package="0402 [SMD]"]
  R11 = Resistor [tolerance=±5% resistance=220 package="0402 [SMD]"]
  R12 = Resistor [tolerance=±5% resistance=220 package="0402 [SMD]"]
  R3 = Resistor [tolerance=±5% resistance=220 package="0402 [SMD]"]

nets:
  N1: Part1.RING2, Part1.TIP, Part2.RING2, Part2.TIP, Part3.RING2, Part3.TIP, Part4.RING2, Part4.TIP, Teensy_3_2.GND, R1.Pin_0, R4.Pin_0, R6.Pin_0, R7.Pin_0, R9.Pin_0, R10.Pin_0, R12.Pin_0, R3.Pin_0
  N2: Teensy_3_2.3V3, R2.Pin_1, R5.Pin_1, R8.Pin_1, R11.Pin_1
  N3: Teensy_3_2.A0/D14, R1.Pin_1, R2.Pin_0, R3.Pin_1
  N4: Teensy_3_2.A1/D15, R4.Pin_1, R5.Pin_0, R6.Pin_1
  N5: Teensy_3_2.A2/D16, R7.Pin_1, R8.Pin_0, R9.Pin_1
  N6: Teensy_3_2.A3/D17, R10.Pin_1, R11.Pin_0, R12.Pin_1
